// Logisim project SAP-1.circ as structural Verilog: 11 circuits, main circuit main
module main (
  input  [3:0] Address,
  input  [7:0] Data,
  input  RUN,
  output [3:0] I7_I4,
  output [3:0] I3_I0
);

  wire and_1_out, and_2_out, Clear_RAM_out, CLK_out, CLR_out, controlled_buffer_1_out,
       Controller_Sequencer_cp, Controller_Sequencer_ea, Controller_Sequencer_ep, Controller_Sequencer_eu,
       Controller_Sequencer_halt, Controller_Sequencer_nei, Controller_Sequencer_nla,
       Controller_Sequencer_nlb, Controller_Sequencer_nli, Controller_Sequencer_nlm,
       Controller_Sequencer_nlo, Controller_Sequencer_su, not_1_out, not_2_out, not_3_out, not_4_out,
       Write_to_RAM_out;
  wire [3:0] Instruction_Register_out_ctrl, MAR_out_ram, multiplexer_1_out, reg_out_1_out_display,
       reg_out_1_out_display_2;
  wire [7:0] ACC_out_add_sub, Reg_B_out_add_sub;

  Button Write_to_RAM (.out(Write_to_RAM_out));
  Button Clear_RAM (.out(Clear_RAM_out));
  Multiplexer #(.width(4), .enable("false")) multiplexer_1 (
    .in0(Address), .in1(MAR_out_ram), .out(multiplexer_1_out), .sel(RUN));
  not not_1 (not_1_out, RUN);
  ProgramCounter PC (
    .Cp(Controller_Sequencer_cp), .nCLK(controlled_buffer_1_out), .CLR(CLR_out), .OUT_BUS(I3_I0),
    .Ep(Controller_Sequencer_ep));
  ControllerSequencer Controller_Sequencer (
    .I4(Instruction_Register_out_ctrl[0]), .I5(Instruction_Register_out_ctrl[1]),
    .I6(Instruction_Register_out_ctrl[2]), .I7(Instruction_Register_out_ctrl[3]),
    .Cp(Controller_Sequencer_cp), .Ep(Controller_Sequencer_ep), .nLm(Controller_Sequencer_nlm),
    .nLi(Controller_Sequencer_nli), .nEi(Controller_Sequencer_nei), .nLa(Controller_Sequencer_nla),
    .Ea(Controller_Sequencer_ea), .Su(Controller_Sequencer_su), .Eu(Controller_Sequencer_eu),
    .nLb(Controller_Sequencer_nlb), .nLo(Controller_Sequencer_nlo), .HALT(Controller_Sequencer_halt));  // open: CLK, nCE
  MemoryAddressRegister MAR (
    .CLK(controlled_buffer_1_out), .IN_BUS(I3_I0), .nLm(Controller_Sequencer_nlm), .CLR(CLR_out),
    .OUT_RAM(MAR_out_ram));
  and and_1 (and_1_out, not_2_out, Write_to_RAM_out);
  and and_2 (and_2_out, not_3_out, Clear_RAM_out);
  not not_2 (not_2_out, RUN);
  not not_3 (not_3_out, RUN);
  InstructionRegister Instruction_Register (
    .nEi(Controller_Sequencer_nei), .CLK(controlled_buffer_1_out), .CLR(CLR_out), .IN_BUS({I7_I4, I3_I0}),
    .nLi(Controller_Sequencer_nli), .OUT_BUS(I3_I0), .OUT_CTRL(Instruction_Register_out_ctrl));
  RAM #(.addrWidth(4), .bus("separate")) ram_1 (
    .addr(multiplexer_1_out), .din(Data), .data({I7_I4, I3_I0}), .str(not_1_out), .clk(and_1_out),
    .clr(and_2_out));  // open: sel, ld
  not not_4 (not_4_out, Controller_Sequencer_halt);
  Button CLR (.out(CLR_out));
  Clock CLK (.out(CLK_out));
  assign controlled_buffer_1_out = not_4_out ? CLK_out : 1'bz;  // Controlled_Buffer controlled_buffer_1
  Hex_Digit_Display hex_digit_display_1 (.value(reg_out_1_out_display_2));  // open: dp
  Hex_Digit_Display hex_digit_display_2 (.value(reg_out_1_out_display));  // open: dp
  Reg_B Reg_B (
    .CLK(controlled_buffer_1_out), .IN_BUS({I7_I4, I3_I0}), .nLb(Controller_Sequencer_nlb), .CLR(CLR_out),
    .OUT_ADD_SUB(Reg_B_out_add_sub));
  Accumulator ACC (
    .CLK(controlled_buffer_1_out), .IN_BUS({I7_I4, I3_I0}), .nLa(Controller_Sequencer_nla), .CLR(CLR_out),
    .OUT_ADD_SUB(ACC_out_add_sub), .Ea(Controller_Sequencer_ea), .OUT_BUS({I7_I4, I3_I0}));
  ADD_SUB ALU (
    .IN_ACC(ACC_out_add_sub), .IN_RegB(Reg_B_out_add_sub), .Su(Controller_Sequencer_su),
    .Eu(Controller_Sequencer_eu));  // open: OUT_BUS
  Reg_Out reg_out_1 (
    .CLK(controlled_buffer_1_out), .IN_BUS({I7_I4, I3_I0}), .nLo(Controller_Sequencer_nlo), .CLR(CLR_out),
    .OUT_Display({reg_out_1_out_display_2, reg_out_1_out_display}));

  // Notes on the sheet:
  //   RAM
endmodule

module ProgramCounter (
  input  Cp,
  input  nCLK,
  input  CLR,
  input  Ep,
  output [3:0] OUT_BUS
);

  wire adder_1_cout, adder_1_out, adder_2_cout, adder_2_out, adder_3_cout, adder_3_out, adder_4_out,
       not_1_out;
  wire [3:0] d_ff_1_q;

  not not_1 (not_1_out, nCLK);
  D_Flip_Flop d_ff_1 (.clk(not_1_out), .D(adder_1_out), .Q(d_ff_1_q[0]), .reset(CLR));  // open: Qn, preset, en
  Adder #(.width(1)) adder_1 (.a(Cp), .b(d_ff_1_q[0]), .out(adder_1_out), .cout(adder_1_cout));  // open: cin
  D_Flip_Flop d_ff_2 (.clk(not_1_out), .D(adder_2_out), .Q(d_ff_1_q[1]), .reset(CLR));  // open: Qn, preset, en
  D_Flip_Flop d_ff_3 (.clk(not_1_out), .D(adder_3_out), .Q(d_ff_1_q[2]), .reset(CLR));  // open: Qn, preset, en
  Adder #(.width(1)) adder_2 (.a(adder_1_cout), .b(d_ff_1_q[1]), .out(adder_2_out), .cout(adder_2_cout));  // open: cin
  D_Flip_Flop d_ff_4 (.clk(not_1_out), .D(adder_4_out), .Q(d_ff_1_q[3]), .reset(CLR));  // open: Qn, preset, en
  Adder #(.width(1)) adder_3 (.a(adder_2_cout), .b(d_ff_1_q[2]), .out(adder_3_out), .cout(adder_3_cout));  // open: cin
  assign OUT_BUS = Ep ? d_ff_1_q : 4'bz;  // Controlled_Buffer controlled_buffer_1
  Adder #(.width(1)) adder_4 (.a(adder_3_cout), .b(d_ff_1_q[3]), .out(adder_4_out));  // open: cin, cout
endmodule

module MemoryAddressRegister (
  input  CLK,
  input  [3:0] IN_BUS,
  input  nLm,
  input  CLR,
  output [3:0] OUT_RAM
);

  wire [3:0] controlled_buffer_1_out;

  assign controlled_buffer_1_out = nLm ? IN_BUS : 4'bz;  // Controlled_Buffer controlled_buffer_1
  D_Flip_Flop d_ff_1 (.clk(CLK), .D(controlled_buffer_1_out[0]), .Q(OUT_RAM[0]), .reset(CLR));  // open: Qn, preset, en
  D_Flip_Flop d_ff_2 (.clk(CLK), .D(controlled_buffer_1_out[1]), .Q(OUT_RAM[1]), .reset(CLR));  // open: Qn, preset, en
  D_Flip_Flop d_ff_3 (.clk(CLK), .D(controlled_buffer_1_out[2]), .Q(OUT_RAM[2]), .reset(CLR));  // open: Qn, preset, en
  D_Flip_Flop d_ff_4 (.clk(CLK), .D(controlled_buffer_1_out[3]), .Q(OUT_RAM[3]), .reset(CLR));  // open: Qn, preset, en
endmodule

module InstructionRegister (
  input  nEi,
  input  CLK,
  input  CLR,
  input  [7:0] IN_BUS,
  input  nLi,
  output [3:0] OUT_BUS,
  output [3:0] OUT_CTRL
);

  wire [3:0] d_ff_2_q;
  wire [7:0] controlled_buffer_1_out;

  assign controlled_buffer_1_out = nLi ? IN_BUS : 8'bz;  // Controlled_Buffer controlled_buffer_1
  D_Flip_Flop d_ff_1 (.clk(CLK), .D(controlled_buffer_1_out[1]), .Q(d_ff_2_q[1]), .reset(CLR));  // open: Qn, preset, en
  D_Flip_Flop d_ff_2 (.clk(CLK), .D(controlled_buffer_1_out[0]), .Q(d_ff_2_q[0]), .reset(CLR));  // open: Qn, preset, en
  D_Flip_Flop d_ff_3 (.clk(CLK), .D(controlled_buffer_1_out[2]), .Q(d_ff_2_q[2]), .reset(CLR));  // open: Qn, preset, en
  D_Flip_Flop d_ff_4 (
    .clk(CLK), .D(controlled_buffer_1_out[3]), .Q(d_ff_2_q[3]), .en(CLR), .reset(CLR));  // open: Qn, preset
  D_Flip_Flop d_ff_5 (.clk(CLK), .D(controlled_buffer_1_out[4]), .Q(OUT_CTRL[0]), .reset(CLR));  // open: Qn, preset, en
  assign OUT_BUS = nEi ? d_ff_2_q : 4'bz;  // Controlled_Buffer controlled_buffer_2
  D_Flip_Flop d_ff_6 (.clk(CLK), .D(controlled_buffer_1_out[5]), .Q(OUT_CTRL[1]), .reset(CLR));  // open: Qn, preset, en
  D_Flip_Flop d_ff_7 (.clk(CLK), .D(controlled_buffer_1_out[6]), .Q(OUT_CTRL[2]), .reset(CLR));  // open: Qn, preset, en
  D_Flip_Flop d_ff_8 (.clk(CLK), .D(controlled_buffer_1_out[7]), .Q(OUT_CTRL[3]), .reset(CLR));  // open: Qn, preset, en
endmodule

module RingCounter (
  input  CLK,
  output T1,
  output T2,
  output T3,
  output T4,
  output T5,
  output T6
);

  wire nor_1_out;

  nor nor_1 (nor_1_out, T1, T2, T3, T4, T5, T6);
  D_Flip_Flop d_ff_1 (.clk(CLK), .D(nor_1_out), .Q(T1));  // open: Qn, preset, en, reset
  D_Flip_Flop d_ff_2 (.clk(CLK), .D(T1), .Q(T2));  // open: Qn, preset, en, reset
  D_Flip_Flop d_ff_3 (.clk(CLK), .D(T2), .Q(T3));  // open: Qn, preset, en, reset
  D_Flip_Flop d_ff_4 (.clk(CLK), .D(T3), .Q(T4));  // open: Qn, preset, en, reset
  D_Flip_Flop d_ff_5 (.clk(CLK), .D(T4), .Q(T5));  // open: Qn, preset, en, reset
  D_Flip_Flop d_ff_6 (.clk(CLK), .D(T5), .Q(T6));  // open: Qn, preset, en, reset
endmodule

module Instruction_Decoder (
  input  I4,
  input  I5,
  input  I6,
  input  I7,
  output LDA,
  output ADD,
  output SUB,
  output OUT,
  output HLT
);

  wire not_1_out, not_2_out, not_3_out, not_4_out, not_5_out, not_6_out, not_7_out, not_8_out, not_9_out;

  not not_1 (not_1_out, I5);
  not not_2 (not_2_out, I6);
  not not_3 (not_3_out, I7);
  not not_4 (not_4_out, I4);
  not not_5 (not_5_out, I6);
  not not_6 (not_6_out, I7);
  not not_7 (not_7_out, I6);
  not not_8 (not_8_out, I7);
  not not_9 (not_9_out, I7);
  and and_1 (LDA, I4, not_1_out, not_2_out, not_3_out);
  and and_2 (ADD, not_4_out, I5, not_5_out, not_6_out);
  and and_3 (SUB, I4, I5, not_7_out, not_8_out);
  and and_4 (OUT, I4, I5, I6, not_9_out);
  and and_5 (HLT, I4, I5, I6, I7);

  // Notes on the sheet:
  //   LDA - 0001
  //   ADD - 0010
  //   SUB - 0011
  //   OUT - 0111
  //   HLT - 1111
  //   N/A - anything else
endmodule

module ControllerSequencer (
  input  CLK,
  input  I4,
  input  I5,
  input  I6,
  input  I7,
  output Cp,
  output Ep,
  output nLm,
  output nCE,
  output nLi,
  output nEi,
  output nLa,
  output Ea,
  output Su,
  output Eu,
  output nLb,
  output nLo,
  output HALT
);

  wire and_1_out, and_2_out, and_3_out, and_4_out, and_5_out, and_6_out, and_7_out, and_8_out, and_9_out,
       and_10_out, and_11_out, and_12_out, and_15_out, and_16_out, and_17_out, and_18_out,
       instruction_decoder_1_add, instruction_decoder_1_lda, instruction_decoder_1_out,
       instruction_decoder_1_sub, ringcounter_1_t3, ringcounter_1_t4, ringcounter_1_t5, ringcounter_1_t6;

  Instruction_Decoder instruction_decoder_1 (
    .I4(I4), .I5(I5), .I6(I6), .I7(I7), .LDA(instruction_decoder_1_lda), .ADD(instruction_decoder_1_add),
    .SUB(instruction_decoder_1_sub), .OUT(instruction_decoder_1_out), .HLT(HALT));
  RingCounter ringcounter_1 (
    .CLK(CLK), .T1(Ep), .T2(Cp), .T3(ringcounter_1_t3), .T4(ringcounter_1_t4), .T5(ringcounter_1_t5),
    .T6(ringcounter_1_t6));
  and and_1 (and_1_out, instruction_decoder_1_add, ringcounter_1_t4);
  and and_2 (and_2_out, instruction_decoder_1_lda, ringcounter_1_t4);
  and and_3 (and_3_out, instruction_decoder_1_lda, ringcounter_1_t5);
  and and_4 (and_4_out, instruction_decoder_1_sub, ringcounter_1_t4);
  nor nor_1 (nLm, and_2_out, and_1_out, and_4_out, Ep);
  and and_5 (and_5_out, instruction_decoder_1_sub, ringcounter_1_t5);
  and and_6 (and_6_out, instruction_decoder_1_add, ringcounter_1_t5);
  nor nor_2 (nCE, and_3_out, and_6_out, and_5_out, ringcounter_1_t3);
  and and_7 (and_7_out, instruction_decoder_1_add, ringcounter_1_t4);
  and and_8 (and_8_out, instruction_decoder_1_lda, ringcounter_1_t4);
  nor nor_3 (nEi, and_8_out, and_7_out, and_9_out);
  not not_1 (nLi, ringcounter_1_t3);
  and and_9 (and_9_out, instruction_decoder_1_sub, ringcounter_1_t4);
  and and_10 (and_10_out, instruction_decoder_1_lda, ringcounter_1_t5);
  and and_11 (and_11_out, instruction_decoder_1_sub, ringcounter_1_t6);
  and and_12 (and_12_out, instruction_decoder_1_add, ringcounter_1_t6);
  nor nor_4 (nLa, and_10_out, and_12_out, and_11_out);
  and and_13 (Su, ringcounter_1_t6, instruction_decoder_1_sub);
  and and_14 (Ea, instruction_decoder_1_out, ringcounter_1_t4);
  and and_15 (and_15_out, ringcounter_1_t6, instruction_decoder_1_add);
  and and_16 (and_16_out, ringcounter_1_t6, instruction_decoder_1_sub);
  or or_1 (Eu, and_15_out, and_16_out);
  and and_17 (and_17_out, ringcounter_1_t5, instruction_decoder_1_sub);
  and and_18 (and_18_out, ringcounter_1_t5, instruction_decoder_1_add);
  nor nor_5 (nLb, and_18_out, and_17_out);
  nand nand_1 (nLo, ringcounter_1_t4, instruction_decoder_1_out);
endmodule

module Accumulator (
  input  CLK,
  input  [7:0] IN_BUS,
  input  nLa,
  input  CLR,
  input  Ea,
  output [7:0] OUT_ADD_SUB,
  output [7:0] OUT_BUS
);

  wire [7:0] controlled_buffer_1_out;

  assign controlled_buffer_1_out = nLa ? IN_BUS : 8'bz;  // Controlled_Buffer controlled_buffer_1
  D_Flip_Flop d_ff_1 (
    .clk(CLK), .D(controlled_buffer_1_out[0]), .Q(OUT_ADD_SUB[0]), .reset(CLR));  // open: Qn, preset, en
  D_Flip_Flop d_ff_2 (
    .clk(CLK), .D(controlled_buffer_1_out[1]), .Q(OUT_ADD_SUB[1]), .reset(CLR));  // open: Qn, preset, en
  D_Flip_Flop d_ff_3 (
    .clk(CLK), .D(controlled_buffer_1_out[3]), .Q(OUT_ADD_SUB[3]), .reset(CLR));  // open: Qn, preset, en
  D_Flip_Flop d_ff_4 (
    .clk(CLK), .D(controlled_buffer_1_out[2]), .Q(OUT_ADD_SUB[2]), .reset(CLR));  // open: Qn, preset, en
  D_Flip_Flop d_ff_5 (
    .clk(CLK), .D(controlled_buffer_1_out[4]), .Q(OUT_ADD_SUB[4]), .reset(CLR));  // open: Qn, preset, en
  D_Flip_Flop d_ff_6 (
    .clk(CLK), .D(controlled_buffer_1_out[5]), .Q(OUT_ADD_SUB[5]), .reset(CLR));  // open: Qn, preset, en
  D_Flip_Flop d_ff_7 (.clk(CLK), .D(controlled_buffer_1_out[6]), .Q(OUT_ADD_SUB[6]));  // open: Qn, preset, en, reset
  assign OUT_BUS = Ea ? OUT_ADD_SUB : 8'bz;  // Controlled_Buffer controlled_buffer_2
  D_Flip_Flop d_ff_8 (
    .clk(CLK), .D(controlled_buffer_1_out[7]), .Q(OUT_ADD_SUB[7]), .reset(CLR));  // open: Qn, preset, en
endmodule

module ADD_SUB (
  input  [7:0] IN_ACC,
  input  [7:0] IN_RegB,
  input  Su,
  input  Eu,
  output [7:0] OUT_BUS
);

  wire [7:0] adder_1_out, multiplexer_1_out, subtractor_1_out;

  Adder adder_1 (.a(IN_ACC), .b(IN_RegB), .out(adder_1_out));  // open: cin, cout
  Subtractor subtractor_1 (.a(IN_ACC), .b(IN_RegB), .out(subtractor_1_out));  // open: bin, bout
  Multiplexer #(.width(8), .enable("false")) multiplexer_1 (
    .in0(adder_1_out), .in1(subtractor_1_out), .out(multiplexer_1_out), .sel(Su));
  assign OUT_BUS = Eu ? multiplexer_1_out : 8'bz;  // Controlled_Buffer controlled_buffer_1
endmodule

module Reg_B (
  input  CLK,
  input  [7:0] IN_BUS,
  input  nLb,
  input  CLR,
  output [7:0] OUT_ADD_SUB
);

  wire [7:0] controlled_buffer_1_out;

  assign controlled_buffer_1_out = nLb ? IN_BUS : 8'bz;  // Controlled_Buffer controlled_buffer_1
  D_Flip_Flop d_ff_1 (
    .clk(CLK), .D(controlled_buffer_1_out[0]), .Q(OUT_ADD_SUB[0]), .reset(CLR));  // open: Qn, preset, en
  D_Flip_Flop d_ff_2 (
    .clk(CLK), .D(controlled_buffer_1_out[1]), .Q(OUT_ADD_SUB[1]), .reset(CLR));  // open: Qn, preset, en
  D_Flip_Flop d_ff_3 (
    .clk(CLK), .D(controlled_buffer_1_out[2]), .Q(OUT_ADD_SUB[2]), .reset(CLR));  // open: Qn, preset, en
  D_Flip_Flop d_ff_4 (
    .clk(CLK), .D(controlled_buffer_1_out[3]), .Q(OUT_ADD_SUB[3]), .reset(CLR));  // open: Qn, preset, en
  D_Flip_Flop d_ff_5 (
    .clk(CLK), .D(controlled_buffer_1_out[4]), .Q(OUT_ADD_SUB[4]), .reset(CLR));  // open: Qn, preset, en
  D_Flip_Flop d_ff_6 (
    .clk(CLK), .D(controlled_buffer_1_out[5]), .Q(OUT_ADD_SUB[5]), .reset(CLR));  // open: Qn, preset, en
  D_Flip_Flop d_ff_7 (.clk(CLK), .D(controlled_buffer_1_out[6]), .Q(OUT_ADD_SUB[6]));  // open: Qn, preset, en, reset
  D_Flip_Flop d_ff_8 (
    .clk(CLK), .D(controlled_buffer_1_out[7]), .Q(OUT_ADD_SUB[7]), .reset(CLR));  // open: Qn, preset, en
endmodule

module Reg_Out (
  input  CLK,
  input  [7:0] IN_BUS,
  input  nLo,
  input  CLR,
  output [7:0] OUT_Display
);

  wire [7:0] controlled_buffer_1_out;

  assign controlled_buffer_1_out = nLo ? IN_BUS : 8'bz;  // Controlled_Buffer controlled_buffer_1
  D_Flip_Flop d_ff_1 (
    .clk(CLK), .D(controlled_buffer_1_out[0]), .Q(OUT_Display[0]), .reset(CLR));  // open: Qn, preset, en
  D_Flip_Flop d_ff_2 (
    .clk(CLK), .D(controlled_buffer_1_out[1]), .Q(OUT_Display[1]), .reset(CLR));  // open: Qn, preset, en
  D_Flip_Flop d_ff_3 (
    .clk(CLK), .D(controlled_buffer_1_out[2]), .Q(OUT_Display[2]), .reset(CLR));  // open: Qn, preset, en
  D_Flip_Flop d_ff_4 (
    .clk(CLK), .D(controlled_buffer_1_out[3]), .Q(OUT_Display[3]), .reset(CLR));  // open: Qn, preset, en
  D_Flip_Flop d_ff_5 (
    .clk(CLK), .D(controlled_buffer_1_out[4]), .Q(OUT_Display[4]), .reset(CLR));  // open: Qn, preset, en
  D_Flip_Flop d_ff_6 (
    .clk(CLK), .D(controlled_buffer_1_out[5]), .Q(OUT_Display[5]), .reset(CLR));  // open: Qn, preset, en
  D_Flip_Flop d_ff_7 (.clk(CLK), .D(controlled_buffer_1_out[6]), .Q(OUT_Display[6]));  // open: Qn, preset, en, reset
  D_Flip_Flop d_ff_8 (
    .clk(CLK), .D(controlled_buffer_1_out[7]), .Q(OUT_Display[7]), .reset(CLR));  // open: Qn, preset, en
endmodule
